# Fritzing sketch motocontrol (saved by Fritzing 1.0.3b)
breadboards: 4

parts:
  U1 = LCD-16X2 [package=lcd-16x2]
  U2 = Carte NUCLEO H755ZI-Q  # not connected
  Sensor1 = TTP223B Capacitive Touch Sensor Module
  Sensor2 = TTP223B Capacitive Touch Sensor Module
  U3 = POT [knob_status=50% power=0.5W package=alps_pot]
  S1 = Pushbutton [package="[THT]"]
  U4 = 74HC04_HEX_INVERTER [package=dil14]  # not connected
  LED1 = RGB LED (com. cathode, rbg) [color="Red (633nm)" current=0.030A package="5 mm [THT]"]
  Mod1 = Passive Buzzer
  U5 = POT [knob_status=50% power=0.5W package=alps_pot]
  R2 = Resistor [tolerance=±5% resistance=220 package="1206 [SMD]"]
  R3 = Resistor [tolerance=±5% resistance=220 package="1206 [SMD]"]
  R4 = Resistor [tolerance=±5% resistance=220 package="1206 [SMD]"]
  R5 = Resistor [tolerance=±5% resistance=220 package="1206 [SMD]"]
  R6 = Resistor [tolerance=±5% resistance=220 package="1206 [SMD]"]
  R7 = Resistor [tolerance=±5% resistance=220 package="1206 [SMD]"]
  R8 = Resistor [tolerance=±5% resistance=220 package="1206 [SMD]"]
  LED3 = LED - 3mm [color="Red (633nm)" current=0.030A package="3 mm [THT]"]
  R9 = Resistor [tolerance=±5% resistance=220 package="1206 [SMD]"]
  VCC1 = 4 x AAA Battery Mount [internal_resistance=0.1Ω]
  R10 = Resistor [tolerance=±5% resistance=220 package="1206 [SMD]"]
  R11 = Resistor [tolerance=±5% resistance=220 package="1206 [SMD]"]
  RY1 = KF-301 Relay [package=THT]
  RY2 = KF-301 Relay [package=THT]
  S2 = Pushbutton [package="[THT]"]
  M1 = DC Motor [voltage_(max)=6V voltage_(min)=3V]
  OMRON2 = OMRON PCB Power Relay – G5LE [part_number="G5LE-1\n" package=THT]  # not connected
  OMRON3 = OMRON PCB Power Relay – G5LE [part_number="G5LE-1\n" package=THT]
  OMRON4 = OMRON PCB Power Relay – G5LE [part_number="G5LE-1\n" package=THT]
  R12 = Resistor [tolerance=±5% resistance=220 package="1206 [SMD]"]
  R13 = Resistor [tolerance=±5% resistance=220 package="1206 [SMD]"]
  R14 = Resistor [tolerance=±5% resistance=150 package="1206 [SMD]"]
  R15 = Resistor [tolerance=±5% resistance=330 package="1206 [SMD]"]
  R16 = Resistor [tolerance=±5% resistance=100 package="1206 [SMD]"]

nets:
  GND: U1.VSS, U1.R_W, U1.DB0, U1.DB1, U1.DB2, U1.DB3, U1.K, Sensor1.GND, Sensor2.GND, U3.E, LED1.common_cathode, Mod1.-, U5.A, R3.Pin_0, R4.Pin_0, R5.Pin_0, R6.Pin_0, R7.Pin_0, R8.Pin_0, LED3.cathode, LED3.anode, R9.Pin_0, R10.Pin_0, R11.Pin_0, RY1.ground, RY2.ground, R12.Pin_0, R13.Pin_0
  VCC: U1.VDD, Sensor1.VCC, Sensor2.VCC, U3.A, S1.Pin_1, S1.Pin_2, Mod1.S, U5.E, R2.Pin_1, RY1.power, RY2.power, S2.Pin_1, S2.Pin_2
  N1: U1.VO, U5.S
  N2: U1.RS, R8.Pin_1
  N3: U1.E, R7.Pin_1
  N4: U1.DB4, R6.Pin_1
  N5: U1.DB5, R5.Pin_1
  N6: U1.DB6, R4.Pin_1
  N7: U1.DB7, R3.Pin_1
  N8: U1.A, R2.Pin_0
  N9: Sensor1.SIG, R11.Pin_1
  N10: Sensor2.SIG, R10.Pin_1
  N11: S1.Pin_3, S1.Pin_4, R12.Pin_1
  N12: LED1.red_anode, R15.Pin_0
  N13: LED1.blue_anode, R14.Pin_0
  N14: LED1.green_anode, R16.Pin_0
  N15: VCC1.+, RY1.C
  N16: RY1.NO, RY2.NC, OMRON3.A, OMRON4.B
  N17: RY2.C, OMRON3.COIL1, OMRON4.COIL2
  N18: RY2.NO, OMRON3.B, OMRON4.A, OMRON4.COIL1
  N19: S2.Pin_3, S2.Pin_4, R13.Pin_1
  N20: M1.pin_1, OMRON4.C
  N21: M1.pin_2, OMRON3.C

custom parts:
  Carte NUCLEO H755ZI-Q: Carte prototype double coeurs ARM
  TTP223B Capacitive Touch Sensor Module: The TTP223B capacitive touch sensor module uses the TTP223B IC. The appropriate voltage is approximately 2 to 5.5 volts.
  KF-301 Relay: KF-301 SPDT Relay module using SRD-05VDC-SL-C relay.
